// Logisim project 8-bit Project.circ as structural Verilog: 4 circuits, main circuit main
module main (
  input  [7:0] in_1,
  input  _2,
  input  [2:0] in_3,
  input  _2_2,
  input  [7:0] in_5,
  input  _0,
  input  _1,
  input  [2:0] in_8,
  output [7:0] out_9,
  output out_10,
  output out_11,
  output out_12,
  output Zero,
  output Negative,
  output Carry,
  output Overflow
);

  wire or_1_out;
  wire [7:0] multiplexer_1_out, multiplexer_2_out, multiplexer_3_out, n8_bit_1_result, n8_bit_and_1_out_3,
       n8_bit_or_1_out_3, shifter_1_out, shifter_2_out;

  Comparator comparator_1 (.a(in_1), .b(shifter_1_out), .gt(out_10), .eq(out_11), .lt(out_12));
  Shifter shifter_1 (.in(in_5), .\dist (in_8), .out(shifter_1_out));
  Shifter #(.shift("lr")) shifter_2 (.in(in_1), .\dist (in_3), .out(shifter_2_out));
  Multiplexer #(.width(8), .enable("false")) multiplexer_1 (
    .in0(in_1), .in1(shifter_2_out), .out(multiplexer_1_out), .sel(_2));
  _8_bit_AND u_8_bit_and_1 (.in_1(multiplexer_1_out), .in_2(shifter_1_out), .out_3(n8_bit_and_1_out_3));
  _8_bit_OR u_8_bit_or_1 (.in_1(multiplexer_1_out), .in_2(shifter_1_out), .out_3(n8_bit_or_1_out_3));
  _8_bit u_8_bit_1 (
    .Add_Sub_Control(_0), .in_2(multiplexer_1_out), .in_3(shifter_1_out), .Result(n8_bit_1_result),
    .Carry_Out(Carry), .Overflow(Overflow));
  Multiplexer #(.width(8), .enable("false")) multiplexer_2 (
    .in0(multiplexer_1_out), .in1(n8_bit_and_1_out_3), .out(multiplexer_2_out), .sel(_2_2));
  Multiplexer #(.width(8), .enable("false")) multiplexer_3 (
    .in0(multiplexer_2_out), .in1(n8_bit_or_1_out_3), .out(multiplexer_3_out), .sel(_0));
  Multiplexer #(.width(8), .enable("false")) multiplexer_4 (
    .in0(multiplexer_3_out), .in1(n8_bit_1_result), .out({Negative, out_9[6:0]}), .sel(_1));
  or or_1 (or_1_out, out_9[0], out_9[1], out_9[2], out_9[3], out_9[4], out_9[5], out_9[6], Negative);
  not not_1 (Zero, or_1_out);

  assign out_9[7] = Negative;
endmodule

// OR
module _8_bit_OR (
  input  [7:0] in_1,
  input  [7:0] in_2,
  output [7:0] out_3
);

  or or_1 (out_3[0], in_1[0], in_2[0]);
  or or_2 (out_3[1], in_1[1], in_2[1]);
  or or_3 (out_3[2], in_1[2], in_2[2]);
  or or_4 (out_3[3], in_1[3], in_2[3]);
  or or_5 (out_3[4], in_1[4], in_2[4]);
  or or_6 (out_3[5], in_1[5], in_2[5]);
  or or_7 (out_3[6], in_1[6], in_2[6]);
  or or_8 (out_3[7], in_1[7], in_2[7]);
endmodule

// AND
module _8_bit_AND (
  input  [7:0] in_1,
  input  [7:0] in_2,
  output [7:0] out_3
);

  and and_1 (out_3[0], in_1[0], in_2[0]);
  and and_2 (out_3[1], in_1[1], in_2[1]);
  and and_3 (out_3[2], in_1[2], in_2[2]);
  and and_4 (out_3[3], in_1[3], in_2[3]);
  and and_5 (out_3[4], in_1[4], in_2[4]);
  and and_6 (out_3[5], in_1[5], in_2[5]);
  and and_7 (out_3[6], in_1[6], in_2[6]);
  and and_8 (out_3[7], in_1[7], in_2[7]);
endmodule

// Add/Sub
module _8_bit (
  input  Add_Sub_Control,
  input  [7:0] in_2,
  input  [7:0] in_3,
  output [7:0] Result,
  output Carry_Out,
  output Overflow
);

  wire adder_1_cout, adder_2_cout, adder_3_cout, adder_4_cout, adder_5_cout, adder_6_cout, adder_7_cout,
       and_1_out, and_2_out, not_1_out, not_2_out, not_3_out, xor_1_out, xor_2_out, xor_3_out, xor_4_out,
       xor_5_out, xor_6_out, xor_7_out, xor_8_out;

  xor xor_1 (xor_1_out, Add_Sub_Control, in_3[0]);
  xor xor_2 (xor_2_out, Add_Sub_Control, in_3[1]);
  xor xor_3 (xor_3_out, Add_Sub_Control, in_3[2]);
  xor xor_4 (xor_4_out, Add_Sub_Control, in_3[3]);
  xor xor_5 (xor_5_out, Add_Sub_Control, in_3[4]);
  xor xor_6 (xor_6_out, Add_Sub_Control, in_3[5]);
  xor xor_7 (xor_7_out, Add_Sub_Control, in_3[6]);
  xor xor_8 (xor_8_out, Add_Sub_Control, in_3[7]);
  not not_1 (not_1_out, xor_8_out);
  not not_2 (not_2_out, in_2[7]);
  Adder #(.width(1)) adder_1 (.a(in_2[0]), .b(xor_1_out), .out(Result[0]), .cin(Add_Sub_Control), .cout(adder_1_cout));
  Adder #(.width(1)) adder_2 (.a(in_2[1]), .b(xor_2_out), .out(Result[1]), .cin(adder_1_cout), .cout(adder_2_cout));
  Adder #(.width(1)) adder_3 (.a(in_2[2]), .b(xor_3_out), .out(Result[2]), .cin(adder_2_cout), .cout(adder_3_cout));
  Adder #(.width(1)) adder_4 (.a(in_2[3]), .b(xor_4_out), .out(Result[3]), .cin(adder_3_cout), .cout(adder_4_cout));
  Adder #(.width(1)) adder_5 (.a(in_2[4]), .b(xor_5_out), .out(Result[4]), .cin(adder_4_cout), .cout(adder_5_cout));
  Adder #(.width(1)) adder_6 (.a(in_2[5]), .b(xor_6_out), .out(Result[5]), .cin(adder_5_cout), .cout(adder_6_cout));
  Adder #(.width(1)) adder_7 (.a(in_2[6]), .b(xor_7_out), .out(Result[6]), .cin(adder_6_cout), .cout(adder_7_cout));
  Adder #(.width(1)) adder_8 (.a(in_2[7]), .b(xor_8_out), .out(Result[7]), .cin(adder_7_cout), .cout(Carry_Out));
  not not_3 (not_3_out, Result[7]);
  and and_1 (and_1_out, Result[7], not_2_out, not_1_out);
  and and_2 (and_2_out, not_3_out, in_2[7], xor_8_out);
  or or_1 (Overflow, and_1_out, and_2_out);
endmodule
